# Fritzing sketch cilamp (saved by Fritzing 0.6.2b)
breadboards: 1

parts:
  Arduino1 = Arduino
  LED1 = Red LED - 5mm [package="5 mm [THT]"]
  R1 = Resistor [tolerance=±5% resistance=220 package=THT]
  R2 = Resistor [tolerance=±5% resistance=220 package=THT]
  LED2 = green LED - 5mm [package="5 mm [THT]"]

nets:
  N1: Arduino1.aref, R1.Pin_1, R2.Pin_1
  N2: Arduino1.D10, LED1.cathode
  N3: Arduino1.D9, LED2.cathode
  N4: LED1.anode, R1.Pin_0
  N5: R2.Pin_0, LED2.anode
